# Fritzing sketch circuito-eletronico-tcc (saved by Fritzing 0.9.10b)
breadboards: 1

parts:
  Componente1 = Arduino Nano (Rev3.0)
  L298N1 = L298N DC motor driver
  DC_Mot_Enc1 = DC Motor with two-phase hall-encoder [part_number=VT-E-G25A-06-177E]
  Componente2 = InvenSense MPU6050
  DC_Mot_Enc2 = DC Motor with two-phase hall-encoder [part_number=VT-E-G25A-06-177E]
  Power_plug1 = Power plug

nets:
  GND: Componente1.GND, Componente2.GND
  N1: Componente1.D2, Componente2.INT
  N2: Componente1.D6, L298N1.ENA
  N3: Componente1.D7, L298N1.IN1
  N4: Componente1.D8, L298N1.IN2
  N5: Componente1.D9, L298N1.ENB
  N6: Componente1.D10, L298N1.IN3
  N7: Componente1.D11/MOSI, L298N1.IN4
  5V: Componente1.5V, Componente2.VCC
  N8: Componente1.A5, Componente2.SCL
  N9: Componente1.A4, Componente2.SDA
  N10: L298N1.OUT1, DC_Mot_Enc1.pin2
  N11: L298N1.OUT2, DC_Mot_Enc1.pin1
  N12: L298N1.OUT3, DC_Mot_Enc2.pin2
  N13: L298N1.OUT4, DC_Mot_Enc2.pin1
  12V: L298N1.12V, Power_plug1.VCC
  GND_2: L298N1.GND, Power_plug1.GND

notes:
  7.4V

custom parts:
  L298N DC motor driver: 2x DC motor driver with 78M05 positive voltage regulator (7..35 V) L298N: max 46 V, 2 A Set 5 V Enable jumper to enable 5 V regultor (needed for the L298N) and +5 V output at screw terminal or supply external +5 V at screw terminal Set ENA and/or ENB to +5 V to enable motor permanently or supply ENA and/or ENB with PWM signal IN1 and IN2 set rotation directory for motor A (OUT1/OUT2) IN2 and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
